# Fritzing sketch QuadBoard (saved by Fritzing 0.9.2b)

parts:
  Part1 = Arduino Mega Proto Shield
  Part2 = 9 Degrees of Freedom - Sensor Stick
  J1 = male pin header, 14 pins [form="♂ (male)"]
  J2 = male pin header, 14 pins [form="♂ (male)"]
  J3 = male pin header, 14 pins [form="♂ (male)"]

nets:
  GND: Part1.GND, Part1.N$56, Part2.GND, J1.pin1, J1.pin2, J1.pin3, J1.pin4, J1.pin5, J1.pin6, J1.pin7, J1.pin8, J1.pin9, J1.pin10, J1.pin11, J1.pin12, J1.pin13, J1.pin14
  N1: Part1.D2, Part1.N$175, J3.pin12
  N2: Part1.D3, Part1.N$180, J3.pin11
  N3: Part1.SCL, Part1.N$54, Part2.SCL
  N4: Part1.SDA, Part1.N$55, Part2.SDA
  N5: Part1.D19, Part1.N$147, J3.pin14
  N6: Part1.D18, Part1.N$152, J3.pin13
  N7: Part1.5V@1, Part1.N$57, Part1.N$148, Part2.VCC, J2.pin14
  N8: Part1.N$1, J2.pin2
  N9: Part1.N$12, J2.pin3
  N10: Part1.N$151, J2.pin13
  N11: Part1.N$176, J2.pin12
  N12: Part1.N$179, J2.pin11
  N13: Part1.N$203, J3.pin10
  N14: Part1.N$204, J2.pin10
  N15: Part1.N$207, J2.pin9
  N16: Part1.N$208, J3.pin9
  N17: Part1.N$231, J3.pin8
  N18: Part1.N$232, J2.pin8
  N19: Part1.N$235, J2.pin7
  N20: Part1.N$236, J3.pin7
  N21: Part1.N$259, J3.pin6
  N22: Part1.N$260, J2.pin6
  N23: Part1.N$263, J2.pin5
  N24: Part1.N$264, J3.pin5
  N25: Part1.N$287, J3.pin4
  N26: Part1.N$288, J2.pin4
  N27: Part1.N$292, J3.pin3
  N28: Part1.N$313, J3.pin2
  N29: Part1.N$337, J3.pin1
  N30: Part1.N$338, J2.pin1
